# Fritzing sketch rover_circuit (saved by Fritzing 0.9.4)
breadboards: 1

parts:
  Rover_Controller = Photon
  H_Bridge = L293D [package=THT]
  Regulator = Voltage Regulator [package=to220-igo]
  V1 = DC Power [voltage=12V]
  C2 = Electrolytic Capacitor [capacitance=1µF package="100 mil [THT, electrolytic]"]
  C3 = Electrolytic Capacitor [capacitance=10µF package="100 mil [THT, electrolytic]"]
  M1 = DC Motor
  M2 = DC Motor
  C4 = Electrolytic Capacitor [capacitance=1µF package="100 mil [THT, electrolytic]"]
  C5 = Electrolytic Capacitor [capacitance=1µF package="100 mil [THT, electrolytic]"]
  C6 = Electrolytic Capacitor [capacitance=1µF package="100 mil [THT, electrolytic]"]
  C7 = Electrolytic Capacitor [capacitance=1µF package="100 mil [THT, electrolytic]"]

nets:
  GND: Rover_Controller.GND, H_Bridge.0V, Regulator.GND, C2.-, C3.-, C4.-, C6.-, C7.-
  N1: Rover_Controller.VIN, H_Bridge.+V, Regulator.OUT, C2.+
  N2: Rover_Controller.D0, H_Bridge.Enable_1
  N3: Rover_Controller.D1, H_Bridge.In_1
  N4: Rover_Controller.D2, H_Bridge.In_2
  N5: Rover_Controller.D3, H_Bridge.Enable_2
  N6: Rover_Controller.D4, H_Bridge.In_3
  N7: Rover_Controller.D5, H_Bridge.In_4
  N8: H_Bridge.Out_1_(_Controlled_by_Enable_1_), M1.pin_1, C6.+
  N9: H_Bridge.Out_2_(_Controlled_by_Enable_1_), M1.pin_2, C7.+
  N10: H_Bridge.+Vmotor, Regulator.IN, V1.V+, C3.+
  N11: H_Bridge.Out_3_(_Controlled_by_Enable_2_), M2.pin_1, C4.+
  N12: H_Bridge.Out_4_(_Controlled_by_Enable_2_), M2.pin_2, C5.+
